// Digital circuit ALU8bits.dig as structural Verilog
module ALU8bits (
  input  [7:0] A,
  input  [7:0] B,
  input  [2:0] Sel,
  input  Chave,
  input  Clock,
  output [7:0] out_4,
  output [7:0] out_5
);

  wire [7:0] A_t, divisor8bits_1_res, MQ, multiplexer_2_out, multiplexer_3_out, multiplicador8bits_1_o,
       nand8bits_1_o, Quo, shift_left8bits_1_o, shift_right8bits_1_o, soma8bits_1_s, subtrator8bits_1_s,
       xor8bits_1_o;

  Multiplexer #(.Bits(8)) multiplexer_1 (.sel(Chave), .in_0(A), .in_1(out_4), .out(A_t));
  soma8bits soma8bits_1 (.A(A_t), .B(B), .S(soma8bits_1_s));  // open: Co
  subtrator8bits subtrator8bits_1 (.A(A_t), .B(B), .S(subtrator8bits_1_s));  // open: Co
  multiplicador8bits multiplicador8bits_1 (.A(A_t), .B(B), .O({MQ, multiplicador8bits_1_o}));
  divisor8bits divisor8bits_1 (.A(A_t), .B(B), .Res(divisor8bits_1_res), .Quo(Quo));
  nand8bits nand8bits_1 (.A(A_t), .B(B), .O(nand8bits_1_o));
  xor8bits xor8bits_1 (.A(A_t), .B(B), .O(xor8bits_1_o));
  shift_left8bits shift_left8bits_1 (.In(A_t), .O(shift_left8bits_1_o));
  shift_right8bits shift_right8bits_1 (.In(A_t), .O(shift_right8bits_1_o));
  Multiplexer #(.Selector_Bits(3), .Bits(8)) multiplexer_2 (
    .sel(Sel), .in_0(soma8bits_1_s), .in_1(subtrator8bits_1_s), .in_2(multiplicador8bits_1_o),
    .in_3(divisor8bits_1_res), .in_4(nand8bits_1_o), .in_5(xor8bits_1_o), .in_6(shift_left8bits_1_o),
    .in_7(shift_right8bits_1_o), .out(multiplexer_2_out));
  Register #(.Bits(8)) AC (.D(multiplexer_2_out), .C(Clock), .en(Clock), .Q(out_4));
  Multiplexer #(.Selector_Bits(3), .Bits(8)) multiplexer_3 (
    .sel(Sel), .in_0({8{1'b0}}), .in_1({8{1'b0}}), .in_2(MQ), .in_3(Quo), .in_4({8{1'b0}}), .in_5({8{1'b0}}),
    .in_6({8{1'b0}}), .in_7({8{1'b0}}), .out(multiplexer_3_out));
  Register #(.Bits(8)) u_MQ (.D(multiplexer_3_out), .C(Clock), .en(Clock), .Q(out_5));

  // Other names for the same wires on the sheet: en = Clock
endmodule
