// Digital circuit CPU8bits.dig as structural Verilog
module CPU8bits (
  input  Clock,
  output [7:0] LSB,
  output [7:0] MSB
);

  wire [2:0] rom_1_d;
  wire [7:0] Counter, ramdualport_1_d;

  contador8bits contador8bits_1 (.C(Clock), .Cnt(Counter));
  ROM #(.AddrBits(8), .Bits(3)) rom_1 (.A(Counter), .sel(1'b1), .D(rom_1_d));
  RAMDualPort #(.AddrBits(8), .Bits(8)) ramdualport_1 (
    .A(Counter), .Din({8{1'b0}}), .str(1'b0), .C(Clock), .ld(1'b1), .D(ramdualport_1_d));
  ALU8bits alu8bits_1 (.A(8'h1), .B(ramdualport_1_d), .Sel(rom_1_d), .Chave(1'b1), .Clock(Clock), .LSB(LSB), .MSB(MSB));

  // Notes on the sheet:
  //   contents of rom_1 (hex, n*v repeats v):
  //   0,1,2
endmodule
