// Digital circuit CPU8bitsHARDCORE.dig as structural Verilog
module CPU8bitsHARDCORE (
  input  Clock,
  input  clk,
  output [7:0] LSB,
  output [7:0] MSB
);

  wire and_1_out, and_2_out, Clock_ALU, Clock_t, comparator_2_eq, Equal, not_1_out, not_2_out, not_3_out, Q;
  wire [7:0] Addr, Counter, multiplexer_1_out, Opcode;
  wire [15:0] D;

  and and_1 (and_1_out, Equal, Q);
  Comparator #(.Bits(8)) comparator_1 (.a(Opcode), .b(8'h9), .eq(Equal));  // open: gt, lt
  CounterPreset #(.maxValue(255), .Bits(8)) counterpreset_1 (
    .en(Q), .C(~Clock_t), .dir(1'b0), .in(Addr), .ld(and_1_out), .clr(1'b0), .out(Counter));  // open: ovf
  not not_1 (not_1_out, Equal);
  and and_2 (and_2_out, Clock, clk);
  not not_2 (not_2_out, comparator_2_eq);
  and and_3 (Clock_t, not_2_out, and_2_out);
  and and_4 (Clock_ALU, Clock_t, not_1_out, Q);
  Comparator #(.Bits(8)) comparator_2 (.a(Opcode), .b(8'h8), .eq(comparator_2_eq));  // open: gt, lt
  T_FF t_ff_1 (.T(1'b1), .C(~Clock_t), .nQ(Q));  // open: Q
  Multiplexer #(.Bits(8)) multiplexer_1 (.sel(Q), .in_0(Counter), .in_1(Addr), .out(multiplexer_1_out));
  not not_3 (not_3_out, Q);
  EEPROMDualPort #(.AddrBits(8), .Bits(16)) eepromdualport_1 (
    .A(multiplexer_1_out), .Din({16{1'b0}}), .str(1'b0), .C(Clock_t), .ld(1'b1), .D(D));
  Register #(.Bits(16)) IR (.D(D), .C(Clock_t), .en(not_3_out), .Q({Opcode, Addr}));
  ALU8bits alu8bits_1 (
    .A({8{1'b0}}), .B(D[7:0]), .Sel(Opcode[2:0]), .Chave(1'b1), .Clock(Clock_ALU), .LSB(LSB), .MSB(MSB));

  // Notes on the sheet:
  //   clk: Hz: 20
endmodule
