// Digital circuit CPU8bitsHARDCOREbus.dig as structural Verilog
module CPU8bitsHARDCOREbus (
  input  Clock,
  output [7:0] LSB,
  output [7:0] MSB
);

  wire and_1_out, Clock_ALU, Clock_t, comparator_1_eq, Equal, Equal8, not_1_out, not_2_out, not_3_out,
       not_4_out, not_5_out, or_1_out, Q, str;
  wire [7:0] Addr, Counter, driver_1_out, Opcode;
  wire [15:0] driver_3_out, eepromdualport_1_d;

  assign driver_1_out = Q ? Addr : 8'bz;  // Driver driver_1
  assign driver_1_out = not_1_out ? Counter : 8'bz;  // Driver driver_2
  not not_1 (not_1_out, Q);
  Multiplexer #(.Bits(8)) multiplexer_1 (.sel(Q), .in_0(Counter), .in_1(Addr));  // open: out
  Comparator #(.Bits(8)) comparator_1 (.a(Opcode), .b(8'hb), .eq(comparator_1_eq));  // open: gt, lt
  and and_1 (and_1_out, Equal, Q);
  and and_2 (str, Q, comparator_1_eq);
  EEPROMDualPort #(.AddrBits(8), .Bits(16)) eepromdualport_1 (
    .A(driver_1_out), .Din(driver_3_out), .str(str), .C(Clock_t), .ld(1'b1), .D(eepromdualport_1_d));
  not not_2 (not_2_out, Equal8);
  and and_3 (Clock_t, not_2_out, Clock);
  not not_3 (not_3_out, str);
  CounterPreset #(.maxValue(255), .Bits(8)) counterpreset_1 (
    .en(Q), .C(~Clock_t), .dir(1'b0), .in(Addr), .ld(and_1_out), .clr(1'b0), .out(Counter));  // open: ovf
  assign driver_3_out = not_3_out ? eepromdualport_1_d : 16'bz;  // Driver driver_3
  Comparator #(.Bits(8)) comparator_2 (.a(Opcode), .b(8'h9), .eq(Equal));  // open: gt, lt
  not not_4 (not_4_out, or_1_out);
  or or_1 (or_1_out, Equal, str);
  Comparator #(.Bits(8)) comparator_3 (.a(Opcode), .b(8'h8), .eq(Equal8));  // open: gt, lt
  not not_5 (not_5_out, Q);
  assign driver_3_out = str ? {MSB, LSB} : 16'bz;  // Driver driver_4
  Register #(.Bits(16)) IR (.D(driver_3_out), .C(Clock_t), .en(not_5_out), .Q({Opcode, Addr}));
  ALU8bits alu8bits_1 (
    .A({8{1'b0}}), .B(driver_3_out[7:0]), .Sel(Opcode[2:0]), .Chave(1'b1), .Clock(Clock_ALU), .LSB(LSB),
    .MSB(MSB));
  and and_4 (Clock_ALU, Clock_t, not_4_out, Q);
  T_FF t_ff_1 (.T(1'b1), .C(~Clock_t), .nQ(Q));  // open: Q

  // Notes on the sheet:
  //   contents of eepromdualport_1 (hex, n*v repeats v):
  //   10,11,b14,905,12,10,b15,800,8*0,a,14,63,0,1e,28
endmodule
