// Digital circuit celula.dig as structural Verilog
module celula (
  input  [7:0] Pin,
  input  [7:0] B,
  input  Ab,
  output [7:0] Po,
  output Qb
);

  wire [7:0] subtrator8bits_1_s;

  subtrator8bits subtrator8bits_1 (.A({Pin[6:0], Ab}), .B(B), .S(subtrator8bits_1_s), .Co(Qb));
  Multiplexer #(.Bits(8)) multiplexer_1 (.sel(Qb), .in_0({Pin[6:0], Ab}), .in_1(subtrator8bits_1_s), .out(Po));
endmodule
