// Digital circuit complemento2.dig as structural Verilog
module complemento2 (
  input  [7:0] In,
  output [7:0] O
);

  wire [7:0] not_1_out;

  not not_1 (not_1_out[0], In[0]);
  not not_2 (not_1_out[1], In[1]);
  not not_3 (not_1_out[2], In[2]);
  not not_4 (not_1_out[3], In[3]);
  not not_5 (not_1_out[4], In[4]);
  not not_6 (not_1_out[5], In[5]);
  not not_7 (not_1_out[6], In[6]);
  not not_8 (not_1_out[7], In[7]);
  soma8bits soma8bits_1 (.A(not_1_out), .B(8'h1), .S(O));  // open: Co
endmodule
