// Digital circuit contador8bits.dig as structural Verilog
module contador8bits (
  input  C,
  output [7:0] Cnt
);

  wire soma8bits_1_co;
  wire [7:0] soma8bits_1_s;

  Register #(.Bits(8)) register_1 (.D(soma8bits_1_s), .C(C), .en(1'b1), .Q(Cnt));
  soma8bits soma8bits_1 (.A(Cnt), .B(8'h1), .S(soma8bits_1_s), .Co(soma8bits_1_co));
  // also tied to GND on the sheet: soma8bits_1_co
endmodule
