// Digital circuit divisor8bits.dig as structural Verilog
module divisor8bits (
  input  [7:0] A,
  input  [7:0] B,
  output [7:0] Res,
  output [7:0] Quo
);

  wire Q3;
  wire [7:0] celula_1_po, celula_2_po, celula_3_po, celula_4_po, celula_5_po, celula_6_po, celula_7_po;

  celula celula_1 (.Pin({8{1'b0}}), .B(B), .Ab(A[7]), .Po(celula_1_po), .Qb(Quo[7]));
  celula celula_2 (.Pin(celula_1_po), .B(B), .Ab(A[6]), .Po(celula_2_po), .Qb(Quo[6]));
  celula celula_3 (.Pin(celula_2_po), .B(B), .Ab(A[5]), .Po(celula_3_po), .Qb(Quo[5]));
  celula celula_4 (.Pin(celula_3_po), .B(B), .Ab(A[4]), .Po(celula_4_po), .Qb(Quo[4]));
  celula celula_5 (.Pin(celula_4_po), .B(B), .Ab(A[3]), .Po(celula_5_po), .Qb(Q3));
  celula celula_6 (.Pin(celula_5_po), .B(B), .Ab(A[2]), .Po(celula_6_po), .Qb(Quo[2]));
  celula celula_7 (.Pin(celula_6_po), .B(B), .Ab(A[1]), .Po(celula_7_po), .Qb(Quo[1]));
  celula celula_8 (.Pin(celula_7_po), .B(B), .Ab(A[0]), .Po(Res), .Qb(Quo[0]));

  assign Quo[3] = Quo[4];

  // Other names for the same wires on the sheet: Q0 = Quo[0]; Q1 = Quo[1]; Q2 = Quo[2]; Q4 = Quo[4]; Q5 = Quo[5];
  //   Q6 = Quo[6]; Q7 = Quo[7]
endmodule
