// Digital circuit divisor8bits_nao_otimizado.dig as structural Verilog
module divisor8bits_nao_otimizado (
  input  [7:0] A,
  input  [7:0] B,
  input  Clock,
  output [7:0] Quo,
  output [7:0] Res
);

  wire comparator_1_eq, comparator_2_eq, comparator_3_eq, comparator_3_gt, Load, not_1_out, not_2_out, R_L,
       RUN;
  wire [7:0] A_t, multiplexer_1_out, Q2, subtrator8bits_1_p3;

  Register #(.Bits(8)) register_1 (.D(A), .C(Clock), .en(1'b1), .Q(A_t));
  Register #(.Bits(8)) register_2 (.D(B), .C(Clock), .en(1'b1), .Q(Q2));
  Comparator #(.Bits(8)) comparator_1 (.a(A), .b(A_t), .eq(comparator_1_eq));  // open: gt, lt
  Comparator #(.Bits(8)) comparator_2 (.a(B), .b(Q2), .eq(comparator_2_eq));  // open: gt, lt
  Comparator #(.Bits(8)) comparator_3 (.a(Res), .b(Q2), .gt(comparator_3_gt), .eq(comparator_3_eq));  // open: lt
  or or_1 (R_L, RUN, Load);
  not not_1 (not_1_out, comparator_1_eq);
  not not_2 (not_2_out, comparator_2_eq);
  Multiplexer #(.Bits(8)) multiplexer_1 (.sel(Load), .in_0(subtrator8bits_1_p3), .in_1(A_t), .out(multiplexer_1_out));
  or or_2 (RUN, comparator_3_gt, comparator_3_eq);
  or or_3 (Load, not_1_out, not_2_out);
  Register #(.Bits(8)) RegA (.D(multiplexer_1_out), .C(Clock), .en(R_L), .Q(Res));
  // subtrator8bits subtrator8bits_1: pin names not known; wires that end beside it: Res, Q2, subtrator8bits_1_p3
  Counter #(.Bits(8)) counter_1 (.en(RUN), .C(Clock), .clr(Load), .out(Quo));  // open: ovf

  // Other names for the same wires on the sheet: Q1[7:0] = Res

  // Notes on the sheet:
  //   Clock: Hz: 64
endmodule
