// Digital circuit divisor8bits_otimizado.dig as structural Verilog
module divisor8bits_otimizado (
  input  [7:0] A,
  input  Load,
  input  [7:0] B,
  input  Clock,
  output [7:0] QUO,
  output [7:0] Resto
);

  wire co, comparator_1_eq, en;
  wire [7:0] counter_1_out, multiplexer_1_out, multiplexer_2_out, mux, subtrator8bits_1_s;

  Counter #(.Bits(8)) counter_1 (.en(en), .C(Clock), .clr(Load), .out(counter_1_out));  // open: ovf
  Multiplexer #(.Bits(8)) multiplexer_1 (.sel(Load), .in_0({QUO[6:0], co}), .in_1(A), .out(multiplexer_1_out));
  Comparator #(.Bits(8)) comparator_1 (.a(counter_1_out), .b(8'h8), .eq(comparator_1_eq));  // open: gt, lt
  Register #(.Bits(8)) RegA (.D(multiplexer_1_out), .C(Clock), .en(en), .Q(QUO));
  not not_1 (en, comparator_1_eq);
  Multiplexer #(.Bits(8)) multiplexer_2 (.sel(Load), .in_0(mux), .in_1({8{1'b0}}), .out(multiplexer_2_out));
  Register #(.Bits(8)) RegP (.D(multiplexer_2_out), .C(Clock), .en(en), .Q(Resto));
  Multiplexer #(.Bits(8)) multiplexer_3 (.sel(co), .in_0({Resto[6:0], QUO[7]}), .in_1(subtrator8bits_1_s), .out(mux));
  subtrator8bits subtrator8bits_1 (.A({Resto[6:0], QUO[7]}), .B(B), .S(subtrator8bits_1_s), .Co(co));

  // Other names for the same wires on the sheet: minuendo[7:0] = {Resto[6:0], QUO[7]}
endmodule
