// Digital circuit multiplicador8bits.dig as structural Verilog
// O(ln n) 8 bit multiplyer
// {{de O(ln n) 8 Bit Multiplizierer}}
module multiplicador8bits (
  input  [7:0] A,
  input  [7:0] B,
  output [15:0] O
);

  wire [7:0] and_1_out, and_9_out, and_17_out, and_25_out, and_33_out, and_41_out, and_49_out, and_57_out;
  wire [15:0] shift_left16bits_1_o, shift_left16bits_2_o, shift_left16bits_3_o, shift_left16bits_4_o,
       shift_left16bits_5_o, shift_left16bits_6_o, shift_left16bits_7_o, shift_left16bits_8_o,
       shift_left16bits_9_o, shift_left16bits_10_o, shift_left16bits_11_o, shift_left16bits_12_o,
       shift_left16bits_13_o, shift_left16bits_14_o, shift_left16bits_15_o, shift_left16bits_16_o,
       shift_left16bits_17_o, shift_left16bits_18_o, shift_left16bits_19_o, shift_left16bits_20_o,
       shift_left16bits_21_o, shift_left16bits_22_o, shift_left16bits_23_o, shift_left16bits_24_o,
       shift_left16bits_25_o, shift_left16bits_26_o, shift_left16bits_27_o, shift_left16bits_28_o,
       somador16bits_1_s, somador16bits_2_s, somador16bits_3_s, somador16bits_4_s, somador16bits_5_s,
       somador16bits_6_s;

  and and_1 (and_1_out[0], A[0], B[0]);
  and and_2 (and_1_out[1], A[1], B[0]);
  and and_3 (and_1_out[2], A[2], B[0]);
  and and_4 (and_1_out[3], A[3], B[0]);
  and and_5 (and_1_out[4], A[4], B[0]);
  and and_6 (and_1_out[5], A[5], B[0]);
  and and_7 (and_1_out[6], A[6], B[0]);
  and and_8 (and_1_out[7], A[7], B[0]);
  and and_9 (and_9_out[0], A[0], B[1]);
  and and_10 (and_9_out[1], A[1], B[1]);
  and and_11 (and_9_out[2], A[2], B[1]);
  and and_12 (and_9_out[3], A[3], B[1]);
  and and_13 (and_9_out[4], A[4], B[1]);
  and and_14 (and_9_out[5], A[5], B[1]);
  and and_15 (and_9_out[6], A[6], B[1]);
  and and_16 (and_9_out[7], A[7], B[1]);
  shift_left16bits shift_left16bits_1 (.In({{8{1'b0}}, and_9_out}), .O(shift_left16bits_1_o));
  somador16bits somador16bits_1 (
    .A(shift_left16bits_1_o), .B({{8{1'b0}}, and_1_out}), .S(somador16bits_1_s));  // open: O
  and and_17 (and_17_out[0], A[0], B[2]);
  and and_18 (and_17_out[1], A[1], B[2]);
  and and_19 (and_17_out[2], A[2], B[2]);
  and and_20 (and_17_out[3], A[3], B[2]);
  and and_21 (and_17_out[4], A[4], B[2]);
  and and_22 (and_17_out[5], A[5], B[2]);
  and and_23 (and_17_out[6], A[6], B[2]);
  and and_24 (and_17_out[7], A[7], B[2]);
  shift_left16bits shift_left16bits_2 (.In({{8{1'b0}}, and_17_out}), .O(shift_left16bits_2_o));
  shift_left16bits shift_left16bits_3 (.In(shift_left16bits_2_o), .O(shift_left16bits_3_o));
  somador16bits somador16bits_2 (.A(shift_left16bits_3_o), .B(somador16bits_1_s), .S(somador16bits_2_s));  // open: O
  and and_25 (and_25_out[0], A[0], B[3]);
  and and_26 (and_25_out[1], A[1], B[3]);
  and and_27 (and_25_out[2], A[2], B[3]);
  and and_28 (and_25_out[3], A[3], B[3]);
  and and_29 (and_25_out[4], A[4], B[3]);
  and and_30 (and_25_out[5], A[5], B[3]);
  and and_31 (and_25_out[6], A[6], B[3]);
  and and_32 (and_25_out[7], A[7], B[3]);
  shift_left16bits shift_left16bits_4 (.In({{8{1'b0}}, and_25_out}), .O(shift_left16bits_4_o));
  shift_left16bits shift_left16bits_5 (.In(shift_left16bits_4_o), .O(shift_left16bits_5_o));
  shift_left16bits shift_left16bits_6 (.In(shift_left16bits_5_o), .O(shift_left16bits_6_o));
  and and_33 (and_33_out[0], A[0], B[4]);
  and and_34 (and_33_out[1], A[1], B[4]);
  and and_35 (and_33_out[2], A[2], B[4]);
  and and_36 (and_33_out[3], A[3], B[4]);
  and and_37 (and_33_out[4], A[4], B[4]);
  and and_38 (and_33_out[5], A[5], B[4]);
  and and_39 (and_33_out[6], A[6], B[4]);
  and and_40 (and_33_out[7], A[7], B[4]);
  somador16bits somador16bits_3 (.A(shift_left16bits_6_o), .B(somador16bits_2_s), .S(somador16bits_3_s));  // open: O
  shift_left16bits shift_left16bits_7 (.In({{8{1'b0}}, and_33_out}), .O(shift_left16bits_7_o));
  shift_left16bits shift_left16bits_8 (.In(shift_left16bits_7_o), .O(shift_left16bits_8_o));
  shift_left16bits shift_left16bits_9 (.In(shift_left16bits_8_o), .O(shift_left16bits_9_o));
  shift_left16bits shift_left16bits_10 (.In(shift_left16bits_9_o), .O(shift_left16bits_10_o));
  and and_41 (and_41_out[0], A[0], B[5]);
  and and_42 (and_41_out[1], A[1], B[5]);
  and and_43 (and_41_out[2], A[2], B[5]);
  and and_44 (and_41_out[3], A[3], B[5]);
  and and_45 (and_41_out[4], A[4], B[5]);
  and and_46 (and_41_out[5], A[5], B[5]);
  and and_47 (and_41_out[6], A[6], B[5]);
  and and_48 (and_41_out[7], A[7], B[5]);
  somador16bits somador16bits_4 (.A(shift_left16bits_10_o), .B(somador16bits_3_s), .S(somador16bits_4_s));  // open: O
  shift_left16bits shift_left16bits_11 (.In({{8{1'b0}}, and_41_out}), .O(shift_left16bits_11_o));
  shift_left16bits shift_left16bits_12 (.In(shift_left16bits_11_o), .O(shift_left16bits_12_o));
  shift_left16bits shift_left16bits_13 (.In(shift_left16bits_12_o), .O(shift_left16bits_13_o));
  shift_left16bits shift_left16bits_14 (.In(shift_left16bits_13_o), .O(shift_left16bits_14_o));
  shift_left16bits shift_left16bits_15 (.In(shift_left16bits_14_o), .O(shift_left16bits_15_o));
  and and_49 (and_49_out[0], A[0], B[6]);
  and and_50 (and_49_out[1], A[1], B[6]);
  and and_51 (and_49_out[2], A[2], B[6]);
  and and_52 (and_49_out[3], A[3], B[6]);
  and and_53 (and_49_out[4], A[4], B[6]);
  and and_54 (and_49_out[5], A[5], B[6]);
  and and_55 (and_49_out[6], A[6], B[6]);
  and and_56 (and_49_out[7], A[7], B[6]);
  somador16bits somador16bits_5 (.A(shift_left16bits_15_o), .B(somador16bits_4_s), .S(somador16bits_5_s));  // open: O
  shift_left16bits shift_left16bits_16 (.In({{8{1'b0}}, and_49_out}), .O(shift_left16bits_16_o));
  shift_left16bits shift_left16bits_17 (.In(shift_left16bits_16_o), .O(shift_left16bits_17_o));
  shift_left16bits shift_left16bits_18 (.In(shift_left16bits_17_o), .O(shift_left16bits_18_o));
  shift_left16bits shift_left16bits_19 (.In(shift_left16bits_18_o), .O(shift_left16bits_19_o));
  shift_left16bits shift_left16bits_20 (.In(shift_left16bits_19_o), .O(shift_left16bits_20_o));
  shift_left16bits shift_left16bits_21 (.In(shift_left16bits_20_o), .O(shift_left16bits_21_o));
  and and_57 (and_57_out[0], A[0], B[7]);
  and and_58 (and_57_out[1], A[1], B[7]);
  and and_59 (and_57_out[2], A[2], B[7]);
  and and_60 (and_57_out[3], A[3], B[7]);
  and and_61 (and_57_out[4], A[4], B[7]);
  and and_62 (and_57_out[5], A[5], B[7]);
  and and_63 (and_57_out[6], A[6], B[7]);
  and and_64 (and_57_out[7], A[7], B[7]);
  somador16bits somador16bits_6 (.A(shift_left16bits_21_o), .B(somador16bits_5_s), .S(somador16bits_6_s));  // open: O
  somador16bits somador16bits_7 (.A(shift_left16bits_28_o), .B(somador16bits_6_s), .S(O));  // open: O
  shift_left16bits shift_left16bits_22 (.In({{8{1'b0}}, and_57_out}), .O(shift_left16bits_22_o));
  shift_left16bits shift_left16bits_23 (.In(shift_left16bits_22_o), .O(shift_left16bits_23_o));
  shift_left16bits shift_left16bits_24 (.In(shift_left16bits_23_o), .O(shift_left16bits_24_o));
  shift_left16bits shift_left16bits_25 (.In(shift_left16bits_24_o), .O(shift_left16bits_25_o));
  shift_left16bits shift_left16bits_26 (.In(shift_left16bits_25_o), .O(shift_left16bits_26_o));
  shift_left16bits shift_left16bits_27 (.In(shift_left16bits_26_o), .O(shift_left16bits_27_o));
  shift_left16bits shift_left16bits_28 (.In(shift_left16bits_27_o), .O(shift_left16bits_28_o));

  // Other names for the same wires on the sheet: Out[15:0] = O
endmodule
