// Digital circuit nand8bits.dig as structural Verilog
module nand8bits (
  input  [7:0] A,
  input  [7:0] B,
  output [7:0] O
);

  wire [7:0] and_1_out;

  assign and_1_out = A & B;  // And and_1, 8 bits wide
  assign O = ~and_1_out;  // Not not_1, 8 bits wide
endmodule
