// Digital circuit soma1bit.dig as structural Verilog
module soma1bit (
  input  A,
  input  B,
  input  Ci,
  output S,
  output Co
);

  wire and_1_out, and_2_out, X1;

  and and_1 (and_1_out, A, B);
  and and_2 (and_2_out, Ci, X1);
  xor xor_1 (X1, A, B);
  or or_1 (Co, and_1_out, and_2_out);
  xor xor_2 (S, X1, Ci);
endmodule
