// Digital circuit soma8bits.dig as structural Verilog
module soma8bits (
  input  [7:0] A,
  input  [7:0] B,
  output [7:0] S,
  output Co
);

  wire soma1bit_1_co, soma1bit_2_co, soma1bit_3_co, soma1bit_4_co, soma1bit_5_co, soma1bit_6_co,
       soma1bit_7_co;

  soma1bit soma1bit_1 (.A(A[0]), .B(B[0]), .Ci(1'b0), .S(S[0]), .Co(soma1bit_1_co));
  soma1bit soma1bit_2 (.A(A[1]), .B(B[1]), .Ci(soma1bit_1_co), .S(S[1]), .Co(soma1bit_2_co));
  soma1bit soma1bit_3 (.A(A[2]), .B(B[2]), .Ci(soma1bit_2_co), .S(S[2]), .Co(soma1bit_3_co));
  soma1bit soma1bit_4 (.A(A[3]), .B(B[3]), .Ci(soma1bit_3_co), .S(S[3]), .Co(soma1bit_4_co));
  soma1bit soma1bit_5 (.A(A[4]), .B(B[4]), .Ci(soma1bit_4_co), .S(S[4]), .Co(soma1bit_5_co));
  soma1bit soma1bit_6 (.A(A[5]), .B(B[5]), .Ci(soma1bit_5_co), .S(S[5]), .Co(soma1bit_6_co));
  soma1bit soma1bit_7 (.A(A[6]), .B(B[6]), .Ci(soma1bit_6_co), .S(S[6]), .Co(soma1bit_7_co));
  soma1bit soma1bit_8 (.A(A[7]), .B(B[7]), .Ci(soma1bit_7_co), .S(S[7]), .Co(Co));
endmodule
