// Digital circuit somador16bits.dig as structural Verilog
module somador16bits (
  input  [15:0] A,
  input  [15:0] B,
  output [15:0] S,
  output O
);

  wire soma1bit_1_co, soma1bit_2_co, soma1bit_3_co, soma1bit_4_co, soma1bit_5_co, soma1bit_6_co,
       soma1bit_7_co, soma1bit_8_co, soma1bit_9_co, soma1bit_10_co, soma1bit_11_co, soma1bit_12_co,
       soma1bit_13_co, soma1bit_14_co, soma1bit_15_co;

  soma1bit soma1bit_1 (.A(A[0]), .B(B[0]), .Ci(1'b0), .S(S[0]), .Co(soma1bit_1_co));
  soma1bit soma1bit_2 (.A(A[1]), .B(B[1]), .Ci(soma1bit_1_co), .S(S[1]), .Co(soma1bit_2_co));
  soma1bit soma1bit_3 (.A(A[2]), .B(B[2]), .Ci(soma1bit_2_co), .S(S[2]), .Co(soma1bit_3_co));
  soma1bit soma1bit_4 (.A(A[3]), .B(B[3]), .Ci(soma1bit_3_co), .S(S[3]), .Co(soma1bit_4_co));
  soma1bit soma1bit_5 (.A(A[4]), .B(B[4]), .Ci(soma1bit_4_co), .S(S[4]), .Co(soma1bit_5_co));
  soma1bit soma1bit_6 (.A(A[5]), .B(B[5]), .Ci(soma1bit_5_co), .S(S[5]), .Co(soma1bit_6_co));
  soma1bit soma1bit_7 (.A(A[6]), .B(B[6]), .Ci(soma1bit_6_co), .S(S[6]), .Co(soma1bit_7_co));
  soma1bit soma1bit_8 (.A(A[7]), .B(B[7]), .Ci(soma1bit_7_co), .S(S[7]), .Co(soma1bit_8_co));
  soma1bit soma1bit_9 (.A(A[8]), .B(B[8]), .Ci(soma1bit_8_co), .S(S[8]), .Co(soma1bit_9_co));
  soma1bit soma1bit_10 (.A(A[9]), .B(B[9]), .Ci(soma1bit_9_co), .S(S[9]), .Co(soma1bit_10_co));
  soma1bit soma1bit_11 (.A(A[10]), .B(B[10]), .Ci(soma1bit_10_co), .S(S[10]), .Co(soma1bit_11_co));
  soma1bit soma1bit_12 (.A(A[11]), .B(B[11]), .Ci(soma1bit_11_co), .S(S[11]), .Co(soma1bit_12_co));
  soma1bit soma1bit_13 (.A(A[12]), .B(B[12]), .Ci(soma1bit_12_co), .S(S[12]), .Co(soma1bit_13_co));
  soma1bit soma1bit_14 (.A(A[13]), .B(B[13]), .Ci(soma1bit_13_co), .S(S[13]), .Co(soma1bit_14_co));
  soma1bit soma1bit_15 (.A(A[14]), .B(B[14]), .Ci(soma1bit_14_co), .S(S[14]), .Co(soma1bit_15_co));
  soma1bit soma1bit_16 (.A(A[15]), .B(B[15]), .Ci(soma1bit_15_co), .S(S[15]), .Co(O));
endmodule
