// Digital circuit subtrator8bits.dig as structural Verilog
module subtrator8bits (
  input  [7:0] A,
  input  [7:0] B,
  output [7:0] S,
  output Co
);

  wire [7:0] complemento2_1_o;

  complemento2 complemento2_1 (.In(B), .O(complemento2_1_o));
  soma8bits soma8bits_1 (.A(A), .B(complemento2_1_o), .S(S), .Co(Co));
endmodule
